// Logisim project 2_input_nor.circ as structural Verilog: 1 circuit, main circuit main
module main (
  input  in_1,
  input  in_2,
  output out_3
);

  wire or_1_out;

  or or_1 (or_1_out, in_1, in_1, in_2, in_2);
  not not_1 (out_3, or_1_out);

  // Notes on the sheet:
  //   2 input NOR
endmodule
