// Logisim project 2_input_or.circ as structural Verilog: 1 circuit, main circuit main
module main (
  input  in_1,
  input  in_2,
  output out_3
);

  or or_1 (out_3, in_1, in_2, in_2);

  // Notes on the sheet:
  //   2 input OR
endmodule
