// Logisim project problem2_circuit_simplified_pos.circ as structural Verilog: 1 circuit, main circuit main
module main (
  input  in_1,
  input  in_2,
  input  in_3,
  input  in_4,
  output out_5
);

  wire not_1_out, not_2_out, not_3_out, or_1_out, or_2_out;

  not not_1 (not_1_out, in_1);
  not not_2 (not_2_out, in_2);
  not not_3 (not_3_out, in_3);
  or or_1 (or_1_out, in_4, not_1_out);
  or or_2 (or_2_out, not_3_out, not_2_out, in_1);
  and and_1 (out_5, not_2_out, or_1_out, or_2_out);
endmodule
